// Logisim project RiskVCPU.circ as structural Verilog: 1 circuit, main circuit RiskVCPU
module RiskVCPU (
  input  SysClk,
  input  Reset,
  input  PCWEn,
  input  [31:0] Instruction
);

  wire ASel, BSel, ebreak, ecall, EX_MEM_ebreak, EX_MEM_ecall, EX_MEM_MemRead, EX_MEM_MemWrite,
       EX_MEM_RegWEn, ID_EX_ASel, ID_EX_BSel, ID_EX_ebreak, ID_EX_ecall, ID_EX_FLUSH, ID_EX_MemRead,
       ID_EX_MemWrite, ID_EX_RegWEn, IF_ID_FLUSH, IF_ID_WE, MEM_WB_ebreak, MEM_WB_ecall, MEM_WB_RegWEn,
       MemRead, MemWrite, PC_WE, PCSel, RegWEn, SysClk_t;
  wire [1:0] AddrOffset, EX_MEM_WBSel, FWD_A, FWD_B, ID_EX_WBSel, MEM_WB_WBSel, WBSel;
  wire [2:0] EX_MEM_MemByteSel, ID_EX_MemByteSel, ImmSel, MemByteSel;
  wire [3:0] StoreMask;
  wire [4:0] ALUSel, BrSel, EX_MEM_rdi, ID_EX_ALUSel, ID_EX_BrSel, ID_EX_rdi, ID_EX_rs1, ID_EX_rs2,
       MEM_WB_rdi, rdi, rs1, rs2;
  wire [6:0] op_code;
  wire [31:0] ALUOut, EX_MEM_ALUOut, EX_MEM_PC, EX_MEM_PC_4, EX_MEM_RDataB, ID_EX_Imm, ID_EX_PC, ID_EX_PC_4,
       ID_EX_RDataA, ID_EX_RDataB, IF_ID_Inst, IF_ID_PC, IF_ID_PC_4, ImmGenOut, Inst, MEM_WB_ALUOut,
       MEM_WB_MemOut, MEM_WB_PC, MEM_WB_PC_4, MEM_WB_RegWBData, MemInAligned, MemOut, MemOutAligned,
       MemWriteData, PC, PCPlus4, RDataA, RDataB, RegWBData;

  Clock clock_1 (.out(SysClk_t));
  // Probe on ALUOut
  // Probe on PC
  // Probe on PCPlus4
  // Probe on Inst
  ProgramCounter programcounter_1 (
    .TargetAddr(ALUOut), .BranchCtl(PCSel), .PCWEn(PC_WE), .Clk(SysClk_t), .Reset(1'b0), .PcOut(PC),
    .PcPlus4(PCPlus4));
  IMem imem_1 (.PC(PC), .Inst(Inst));
  // Probe on IF_ID_PC
  IF_ID if_id_1 (
    .Inst(Inst), .PC(PC), .PCPlus4(PCPlus4), .IF_ID_WE(IF_ID_WE), .IF_ID_FLUSH(IF_ID_FLUSH),
    .SysClk(SysClk_t), .IF_ID_Inst(IF_ID_Inst), .IF_ID_PC(IF_ID_PC), .IF_ID_PC_4(IF_ID_PC_4));
  // Probe on ImmGenOut
  // Probe on RDataA
  // Probe on RDataB
  // Probe on RegWBData
  // MainController maincontroller_1: pin names not known; wires that end beside it: IF_ID_Inst, ImmSel, ASel, BSel, ALUSel, BrSel, MemRead, MemWrite, MemByteSel, RegWEn, WBSel, ecall, ebreak, rdi, rs1, rs2, op_code
  ImmGen immgen_1 (.InstIn(IF_ID_Inst), .ImmSelIn(ImmSel), .ImmOut(ImmGenOut));
  RegisterFile registerfile_1 (
    .Data(MEM_WB_RegWBData), .RdAddr(MEM_WB_rdi), .Rs1Addr(rs1), .Rs2Addr(rs2), .WriteEnable(MEM_WB_RegWEn),
    .Clk(SysClk_t), .DataA(RDataA), .DataB(RDataB));
  // Probe on ImmSel
  // Probe on ASel
  // Probe on BSel
  // Probe on ALUSel
  // Probe on BrSel
  // Probe on MemRead
  // Probe on MemWrite
  // Probe on MemByteSel
  // Probe on RegWEn
  // Probe on WBSel
  // Probe on ecall
  // Probe on ebreak
  // Probe on rdi
  // Probe on rs1
  // Probe on rs2
  ID_EX id_ex_1 (
    .RDataA(RDataA), .RDataB(RDataB), .Imm(ImmGenOut), .ASel(ASel), .BSel(BSel), .ALUSel(ALUSel),
    .BrSel(BrSel), .MemRead(MemRead), .MemWrite(MemWrite), .MemByteSel(MemByteSel), .RegWEn(RegWEn),
    .WBSel(WBSel), .ecall(ecall), .ebreak(ebreak), .rdi(rdi), .rs1(rs1), .rs2(rs2), .IF_ID_PC(IF_ID_PC),
    .IF_ID_PC_4(IF_ID_PC_4), .ID_EX_FLUSH(ID_EX_FLUSH), .SysClk(SysClk_t), .ID_EX_RDataA(ID_EX_RDataA),
    .ID_EX_RDataB(ID_EX_RDataB), .ID_EX_Imm(ID_EX_Imm), .ID_EX_ASel(ID_EX_ASel), .ID_EX_BSel(ID_EX_BSel),
    .ID_EX_ALUSel(ID_EX_ALUSel), .ID_EX_BrSel(ID_EX_BrSel), .ID_EX_MemRead(ID_EX_MemRead),
    .ID_EX_MemWrite(ID_EX_MemWrite), .ID_EX_MemByteSel(ID_EX_MemByteSel), .ID_EX_RegWEn(ID_EX_RegWEn),
    .ID_EX_WBSel(ID_EX_WBSel), .ID_EX_ecall(ID_EX_ecall), .ID_EX_ebreak(ID_EX_ebreak), .ID_EX_rdi(ID_EX_rdi),
    .ID_EX_rs1(ID_EX_rs1), .ID_EX_rs2(ID_EX_rs2), .ID_EX_PC(ID_EX_PC), .ID_EX_PC_4(ID_EX_PC_4));
  // Probe on PCSel
  // Probe on ALUOut
  // HazardControl hazardcontrol_1: pin names not known; wires that end beside it: PCSel, rs1, rs2, ID_EX_rs1, ID_EX_rs2, ID_EX_rdi, PC_WE, IF_ID_WE, IF_ID_FLUSH, ID_EX_FLUSH, FWD_A, FWD_B
  BranchController branchcontroller_1 (
    .dataA(ID_EX_RDataA), .dataB(ID_EX_RDataB), .BrSel(ID_EX_BrSel), .TakeBranch(PCSel));
  ALUControl alucontrol_1 (
    .RDataA(ID_EX_RDataA), .PC(ID_EX_PC), .ASel(ID_EX_ASel), .RDataB(ID_EX_RDataB), .ImmVal(ID_EX_Imm),
    .BSel(ID_EX_BSel), .ALUSel(ID_EX_ALUSel), .EX_MEM_ALUOut(EX_MEM_ALUOut), .MEM_WB_ALUOut(MEM_WB_MemOut),
    .FWD_A(FWD_A), .FWD_B(FWD_B), .DataOut(ALUOut));
  EX_MEM ex_mem_1 (
    .ALUOut(ALUOut), .ID_EX_RDataB(ID_EX_RDataB), .ID_EX_MemRead(ID_EX_MemRead),
    .ID_EX_MemWrite(ID_EX_MemWrite), .ID_EX_MemByteSel(ID_EX_MemByteSel), .ID_EX_RegWEn(ID_EX_RegWEn),
    .ID_EX_WBSel(ID_EX_WBSel), .ID_EX_ecall(ID_EX_ecall), .ID_EX_ebreak(ID_EX_ebreak), .ID_EX_rdi(ID_EX_rdi),
    .ID_EX_PC(ID_EX_PC), .ID_EX_PC_4(ID_EX_PC_4), .SysClk(SysClk_t), .EX_MEM_ALUOut(EX_MEM_ALUOut),
    .EX_MEM_RDataB(EX_MEM_RDataB), .EX_MEM_MemRead(EX_MEM_MemRead), .EX_MEM_MemWrite(EX_MEM_MemWrite),
    .EX_MEM_MemByteSel(EX_MEM_MemByteSel), .EX_MEM_RegWEn(EX_MEM_RegWEn), .EX_MEM_WBSel(EX_MEM_WBSel),
    .EX_MEM_ecall(EX_MEM_ecall), .EX_MEM_ebreak(EX_MEM_ebreak), .EX_MEM_rdi(EX_MEM_rdi),
    .EX_MEM_PC(EX_MEM_PC), .EX_MEM_PC_4(EX_MEM_PC_4));
  // Probe on MemWriteData
  // Probe on EX_MEM_RDataB
  // Probe on AddrOffset
  // Probe on MemOut
  // Probe on MemInAligned
  // Probe on MemOutAligned
  // Probe on AddrOffset
  DMem dmem_1 (
    .MemAddr(EX_MEM_ALUOut), .MemWrite(EX_MEM_MemWrite), .MemRead(EX_MEM_MemRead), .StoreMast(StoreMask),
    .clk(SysClk_t), .WriteData(MemWriteData), .AddrOffset(AddrOffset), .MemOut(MemOut));
  StoreAligner storealigner_1 (
    .Data(EX_MEM_RDataB), .AddrOffset(AddrOffset), .ByteSel(EX_MEM_MemByteSel), .DataOut(MemWriteData),
    .MaskOut(StoreMask));
  LoadAligner loadaligner_1 (.AddrOffset(AddrOffset), .Data(MemOut), .ByteSel(EX_MEM_MemByteSel), .Out0(MemOutAligned));
  MEM_WB mem_wb_1 (
    .MemData(MemOutAligned), .EX_MEM_ALUOut(EX_MEM_ALUOut), .EX_MEM_RegWEn(EX_MEM_RegWEn),
    .EX_MEM_WBSel(EX_MEM_WBSel), .EX_MEM_ecall(EX_MEM_ecall), .EX_MEM_ebreak(EX_MEM_ebreak),
    .EX_MEM_rdi(EX_MEM_rdi), .EX_MEM_PC(EX_MEM_PC), .EX_MEM_PC_4(EX_MEM_PC_4), .SysClk(SysClk_t),
    .MEM_WB_MemOut(MEM_WB_MemOut), .MEM_WB_ALUOut(MEM_WB_ALUOut), .MEM_WB_RegWEn(MEM_WB_RegWEn),
    .MEM_WB_WBSel(MEM_WB_WBSel), .MEM_WB_ecall(MEM_WB_ecall), .MEM_WB_ebreak(MEM_WB_ebreak),
    .MEM_WB_rdi(MEM_WB_rdi), .MEM_WB_PC(MEM_WB_PC), .MEM_WB_PC_4(MEM_WB_PC_4));
  // Probe on MEM_WB_WBSel
  // Probe on MEM_WB_RegWBData
  WriteBackControl writebackcontrol_1 (
    .ALUOut(MEM_WB_ALUOut), .MemOut(MEM_WB_MemOut), .PCPlus4(MEM_WB_PC_4), .WBSel(MEM_WB_WBSel),
    .OutData(MEM_WB_RegWBData));

  // Notes on the sheet:
  //   IF - Instruction Fetch
  //   IF_ID
  //   ID - Instruction Decode
  //   ID_EX
  //   EX - Execute
  //   EX_MEM
  //   MEM - Memory
  //   MEM_WB
  //   00 = ALU
  //   01 = Mem
  //   11 = PCPlus4
  //   WB - Write Back
endmodule
